# Fritzing sketch diagrama_control_motores (saved by Fritzing 0.9.2b)
breadboards: 1

parts:
  Part1 = Arduino Uno (Rev3)
  M1 = DC Motor
  IC1 = ULN2003A [package="DIP16 [THT]"]

nets:
  N1: Part1.D9_PWM, IC1.In_1
  N2: Part1.5V, M1.pin_1, IC1.COM_-_Common
  N3: Part1.GND, IC1.0V
  N4: M1.pin_2, IC1.Out_1

notes:
  Stepper Driver Motor
